# Fritzing sketch 2019 11 12 Компоновка (saved by Fritzing 0.9.3b)
circuit board: 8.46667cm x 5.64444cm
stripboards: 1
perfboards: 1

parts:
  Power_plug = Power plug
  Часть2 = DC Step Down from 24/12V to 5V USB 5A [part_number=XY-3606]
  U1 = LM2596 step down module
  R4 = Resistor [tolerance=±5% resistance=1k package=THT]
  C4 = Electrolytic Capacitor [capacitance=0.1mF voltage=16V package="100 mil [THT, electrolytic]"]
  Input_Gnd_+12V = female pin header, 2 pins [form="♀ (female)"]
  Fan_control = female pin header, 1 pin [form="♀ (female)"]
  Fan_Gnd_+12V = female pin header, 2 pins [form="♀ (female)"]
  D4 = Rectifier Diode [part_number=1N4007 package="300 mil [THT]"]
  Q5 = npn-Powertransistor [package="TO220 [THT]"]
  Часть6 = Arduino Nano (Rev3.0)
  Raspberry_Pi_2 = Raspberry Pi 3 [part_number=RPI-3-V1.2]
  PEN = female pin header, 1 pin [form="♀ (female)" part_number=pin]
  C5 = Ceramic Capacitor [capacitance=0.1mF voltage=0.1kV package="100 mil [THT, multilayer]"]
  INA226 = INA226 Sensor
  GND_3V3_SDA_SCL = female pin header, 4 pins [form="♀ (female)" part_number="Sensors Interface"]
  C6 = Ceramic Capacitor [capacitance=0.1mF voltage=0.1kV package="100 mil [THT, multilayer]"]

nets:
  GND: Power_plug.GND, Часть2.IN-, Часть2.OUT-, U1.IN-, Input_Gnd_+12V.pin1, Fan_Gnd_+12V.pin1, D4.cathode, Часть6.GND, Raspberry_Pi_2.GND, C5.1, INA226.GND, GND_3V3_SDA_SCL.pin1, C6.0
  N1: Power_plug.VCC, INA226.VBS, INA226.Rin+
  N2: Часть2.IN+24/12VDC, U1.IN+, C4.-, Input_Gnd_+12V.pin2, Q5.emitter, INA226.Rin-
  5V: Часть2.OUT+5VDC, Часть6.5V, Raspberry_Pi_2.5V, C6.1
  N3: U1.OUT+, C5.0, INA226.VCC, GND_3V3_SDA_SCL.pin2
  N4: R4.Pin_0, C4.+, Q5.base
  N5: R4.Pin_1, Fan_control.pin1, Часть6.D3
  N6: Fan_Gnd_+12V.pin2, D4.anode, Q5.collector
  N7: Часть6.D8, Raspberry_Pi_2.GIPO4
  N8: Часть6.D9, PEN.pin1
  N9: Часть6.A5, INA226.SCL, GND_3V3_SDA_SCL.pin4
  N10: Часть6.A4, INA226.SDA, GND_3V3_SDA_SCL.pin3
  N11: INA226.IN-, INA226.ALE

custom parts:
  LM2596 step down module: LM2596 DC-DC step down power supply module 3 A.
  INA226 Sensor: Current, voltage and power sensor via I2C protocol
