# Fritzing sketch TCA9548A_multiplexer (saved by Fritzing 0.9.3b)
circuit board: 7.02029cm x 4.78378cm
stripboards: 1

parts:
  R1 = Resistor [tolerance=±5% resistance=10k package=THT]
  R2 = Resistor [tolerance=±5% resistance=4.7k package=THT]
  R4 = Resistor [tolerance=±5% resistance=4.7k package=THT]
  R3 = Resistor [tolerance=±5% resistance=4.7k package=THT]
  R5 = Resistor [tolerance=±5% resistance=4.7k package=THT]
  R6 = Resistor [tolerance=±5% resistance=4.7k package=THT]
  R7 = Resistor [tolerance=±5% resistance=4.7k package=THT]
  R8 = Resistor [tolerance=±5% resistance=4.7k package=THT]
  R9 = Resistor [tolerance=±5% resistance=4.7k package=THT]
  R10 = Resistor [tolerance=±5% resistance=4.7k package=THT]
  R11 = Resistor [tolerance=±5% resistance=4.7k package=THT]
  R12 = Resistor [tolerance=±5% resistance=4.7k package=THT]
  R13 = Resistor [tolerance=±5% resistance=4.7k package=THT]
  R14 = Resistor [tolerance=±5% resistance=4.7k package=THT]
  R15 = Resistor [tolerance=±5% resistance=4.7k package=THT]
  R16 = Resistor [tolerance=±5% resistance=4.7k package=THT]
  R17 = Resistor [tolerance=±5% resistance=4.7k package=THT]
  +3_3V = male pin header, 4 pins [form="♂ (male)"]
  C6 = Ceramic Capacitor [capacitance=100nF voltage=0.1kV package="100 mil [THT, multilayer]"]
  J10 = male pin header, 8 pins [form="♂ (male)"]
  J11 = male pin header, 8 pins [form="♂ (male)"]
  Part2 = Adafruit TCA9548A
  J2 = male pin header, 4 pins [form="♂ (male)"]
  J9 = male pin header, 12 pins [form="♂ (male)"]

nets (from the schematic view):
  N1: R1.Pin_0, Part2.RESET
  N2: R1.Pin_1, R2.Pin_0, R4.Pin_0, R3.Pin_0, R5.Pin_0, R6.Pin_0, R7.Pin_0, R8.Pin_0, R9.Pin_0, R10.Pin_0, R11.Pin_0, R12.Pin_0, R13.Pin_0, R14.Pin_0, R15.Pin_0, R16.Pin_0, R17.Pin_0, +3_3V.pin1, C6.1, J10.pin1, J10.pin2, J10.pin3, J10.pin4, J10.pin5, J10.pin6, J10.pin7, J10.pin8, Part2.VCC
  N3: R2.Pin_1, Part2.2SDA, J9.pin1
  N4: R4.Pin_1, Part2.3SDA, J9.pin3
  N5: R3.Pin_1, Part2.2SCL, J9.pin2
  N6: R5.Pin_1, Part2.3SCL, J9.pin4
  N7: R6.Pin_1, Part2.4SDA, J9.pin5
  N8: R7.Pin_1, Part2.4SCL, J9.pin6
  N9: R8.Pin_1, Part2.5SDA, J9.pin7
  N10: R9.Pin_1, Part2.5SCL, J9.pin8
  N11: R10.Pin_1, Part2.6SDA, J9.pin9
  N12: R11.Pin_1, Part2.6SCL, J9.pin10
  N13: R12.Pin_1, Part2.7SDA, J9.pin11
  N14: R13.Pin_1, Part2.7SCL, J9.pin12
  N15: R14.Pin_1, Part2.0SDA, J2.pin1
  N16: R15.Pin_1, Part2.0SCL, J2.pin2
  N17: R16.Pin_1, Part2.1SDA, J2.pin3
  N18: R17.Pin_1, Part2.1SCL, J2.pin4
  N19: +3_3V.pin2, C6.0, J11.pin1, J11.pin2, J11.pin3, J11.pin4, J11.pin5, J11.pin6, J11.pin7, J11.pin8, Part2.GND, Part2.A0, Part2.A1, Part2.A2
  N20: +3_3V.pin3, Part2.INPUTSDA
  N21: +3_3V.pin4, Part2.INPUTSCL

custom parts:
  Adafruit TCA9548A: You just found the perfect I2C sensor, and you want to wire up two or three or more of them to your Arduino when you realize "Uh oh, this chip has a fixed I2C address, and from what I know about I2C, you cannot have two devices with the same address on the same SDA/SCL pins!" Are you out of luck? You would be, if you didn't have this ultra-cool TCA9548A 1-to-8 I2C multiplexer! Finally, a way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
