# Fritzing sketch layout (saved by Fritzing 0.9.3b)
perfboards: 2

parts:
  J10 = female pin header, 4 pins [form="♀ (female)" part_number="12V, GND, SDA, SCL"]
  J11 = female pin header, 1 pin [form="♀ (female)" part_number=5V]
  J12 = female pin header, 1 pin [form="♀ (female)" part_number=3V3]
  J13 = female pin header, 2 pins [form="♀ (female)" part_number="In, Out"]
  J14 = female pin header, 4 pins [form="♀ (female)" part_number="3V3, GND, SDA, SCL"]
  J15 = female pin header, 2 pins [form="♀ (female)"]  # not connected
  J16 = female pin header, 2 pins [form="♀ (female)"]  # not connected
  J17 = female pin header, 4 pins [form="♀ (female)"]  # not connected
  J18 = female pin header, 4 pins [form="♀ (female)"]  # not connected
  DC_Downstep_3_8V1 = LM2596 step down module
  DC_Downstep_5V1 = DC Step Down from 24/12V to 5V USB 5A [part_number=XY-3606]
  Power1 = Screw terminal - 2 pins [part_number="GND, +12V" package=THT]

nets:
  N1: J10.pin1, J13.pin1, DC_Downstep_3_8V1.IN+, DC_Downstep_5V1.IN+24/12VDC
  N2: J10.pin2, J14.pin2, DC_Downstep_3_8V1.IN-, DC_Downstep_5V1.IN-, DC_Downstep_5V1.OUT-, Power1.pin1
  N3: J10.pin3, J14.pin3
  N4: J10.pin4, J14.pin4
  N5: J11.pin1, DC_Downstep_5V1.OUT+5VDC
  N6: J12.pin1, J14.pin1, DC_Downstep_3_8V1.OUT+
  N7: J13.pin2, Power1.pin2

custom parts:
  LM2596 step down module: LM2596 DC-DC step down power supply module 3 A.
